# Fritzing sketch schematic (saved by Fritzing 0.9.6b)

parts:
  Screen = 2.8" SPI TFT Module [part_number=ILI9341]
  Pi_Pico = Raspberry Pi Pico
  DAC = Adafruit MAX98357A I2S 3W Class D Amplifier [part_number=MAX98357A]
  FIRE = Pushbutton [package="[THT]"]
  ESC = Pushbutton [package="[THT]"]
  ENTER = Pushbutton [package="[THT]"]
  OPEN = Pushbutton [package="[THT]"]
  LEFT = Pushbutton [package="[THT]"]
  UP = Pushbutton [package="[THT]"]
  RIGHT = Pushbutton [package="[THT]"]
  DOWN = Pushbutton [package="[THT]"]

nets:
  N1: Screen.pin1, Pi_Pico.pin_36, DAC.VIN
  N2: Screen.pin2, Pi_Pico.pin_8, Pi_Pico.pin_18, Pi_Pico.pin_38, DAC.GND, FIRE.Pin_3, FIRE.Pin_4, ESC.Pin_3, ESC.Pin_4, ENTER.Pin_4, OPEN.Pin_3, OPEN.Pin_4, LEFT.Pin_3, LEFT.Pin_4, UP.Pin_3, UP.Pin_4, RIGHT.Pin_3, RIGHT.Pin_4, DOWN.Pin_3, DOWN.Pin_4
  N3: Screen.pin3, Pi_Pico.pin_22
  N4: Screen.pin4, Pi_Pico.pin_27
  N5: Screen.pin5, Pi_Pico.pin_26
  N6: Screen.pin6, Pi_Pico.pin_25
  N7: Screen.pin7, Pi_Pico.pin_24
  N8: Screen.pin8, Pi_Pico.pin_29
  N9: Pi_Pico.pin_1, ESC.Pin_1, ESC.Pin_2
  N10: Pi_Pico.pin_4, FIRE.Pin_1, FIRE.Pin_2
  N11: Pi_Pico.pin_5, OPEN.Pin_1, OPEN.Pin_2
  N12: Pi_Pico.pin_6, ENTER.Pin_1, ENTER.Pin_2
  N13: Pi_Pico.pin_7, DOWN.Pin_1, DOWN.Pin_2
  N14: Pi_Pico.pin_9, RIGHT.Pin_1, RIGHT.Pin_2
  N15: Pi_Pico.pin_11, LEFT.Pin_1, LEFT.Pin_2
  N16: Pi_Pico.pin_12, UP.Pin_1, UP.Pin_2
  N17: Pi_Pico.pin_31, DAC.BCLK
  N18: Pi_Pico.pin_32, DAC.LRCLK
  N19: Pi_Pico.pin_34, DAC.DIN

custom parts:
  2.8" SPI TFT Module: A generic 2.8 inch LCD TFT 320x240 display with touchscreen and SD card slot. Uses the ILI9341 controller, like the Adafruit displays of this size uses.
  Raspberry Pi Pico: Raspberry Pi Pico. Based around the RP2040 microcontroller the Pico is a low cost microcontroller device bringing Raspberry Pi quality, cost, and easy of use to the microcontroller space. Jan 2021, Split part in to two versions: tht (this one) and SMD. This one will drill holes for a .1 in header in pcb to allow plugging in the module as well as providing pads to solder the module to the top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
  Adafruit MAX98357A I2S 3W Class D Amplifier: Listen to this good news - we now have an all in one digital audio amp breakout board that works incredibly well with the Raspberry Pi! If you're looking for an easy and low cost way to get you digital sound files bumpin' then the MAX08357 I2S Amp Breakout is for you. It takes standard I2S digital audio input and, not only decodes it into analog, but also amplifies it directly into a speaker.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
